# Fritzing sketch Wiring Diagram (saved by Fritzing 0.9.3b)
breadboards: 1

parts:
  hc-sr1 = hc-sr04
  R1 = PHOTOCELL [package=photocell]
  R2 = PHOTOCELL [package=photocell]
  R3 = Resistor [tolerance=±5% resistance=220 package=THT]
  R4 = Resistor [tolerance=±5% resistance=220 package=THT]
  J1 = Basic Servo
  J2 = Basic Servo
  Part1 = Arduino Uno (Rev3) - ICSP

nets:
  VCC: hc-sr1.VCC, R1.P$2, R2.P$1, J1.vcc, J2.vcc, Part1.5V
  N1: hc-sr1.Trig, Part1.D4
  N2: hc-sr1.Echo, Part1.D5_PWM
  GND: hc-sr1.GND, R3.Pin_1, R4.Pin_0, J1.gnd, J2.gnd, Part1.GND
  N3: R1.P$1, R3.Pin_0, Part1.A5/SCL
  N4: R2.P$2, R4.Pin_1, Part1.A4/SDA
  N5: J1.pulse, Part1.D12/MISO
  N6: J2.pulse, Part1.D11_PWM/MOSI
